// Logisim project FSMcompletosincronodef.circ as structural Verilog: 1 circuit, main circuit main
module main (
);

  wire A1_out, A2_out, A3_out, A4_out, clock_1_out, Enable_out, O1_out, Q0_q, Q0_qn, Q1_q, Q1_qn, Q2_q,
       U1_out;

  Clock clock_1 (.out(clock_1_out));
  Button Enable (.out(Enable_out));
  nand U1 (U1_out, Enable_out, Enable_out);
  or O1 (O1_out, Q1_q, U1_out);
  and A1 (A1_out, Q0_qn, O1_out);
  and A4 (A4_out, Q0_qn, Enable_out);
  D_Flip_Flop Q0 (.clk(clock_1_out), .D(A1_out), .Q(Q0_q), .Qn(Q0_qn));  // open: preset, en, reset
  D_Flip_Flop Q1 (.clk(clock_1_out), .D(A4_out), .Q(Q1_q), .Qn(Q1_qn));  // open: preset, en, reset
  D_Flip_Flop Q2 (.clk(clock_1_out), .D(Enable_out), .Q(Q2_q));  // open: Qn, preset, en, reset
  and A2 (A2_out, Q1_qn, Q0_qn);
  and A3 (A3_out, A2_out, Q2_q);
  LED LV (.in(Q1_q));
  LED LG (.in(Q0_q));
  LED LR (.in(A3_out));

  // Notes on the sheet:
  //   D0 = (E'+Q1).Q0'
  //   D1=Q0'.E
  //   D2=E
  //   LV=Q1
  //   LG=Q0
  //   LR=(Q0'.Q1').Q2
endmodule
